# Fritzing sketch lora_send_receive (saved by Fritzing 0.9.3b)

parts:
  WeMos_D1_Mini1 = WeMos D1 Mini
  RFM95W1 = RFM95W LoRa Module

nets:
  N1: WeMos_D1_Mini1.3V3, RFM95W1.13_3.3V
  N2: WeMos_D1_Mini1.D1, RFM95W1.15_DIO1
  N3: WeMos_D1_Mini1.D2, RFM95W1.16_DIO2
  N4: WeMos_D1_Mini1.D3, RFM95W1.11_DIO3
  N5: WeMos_D1_Mini1.D4, RFM95W1.12_DIO4
  N6: WeMos_D1_Mini1.D6, RFM95W1.4_SCK
  N7: WeMos_D1_Mini1.D7, RFM95W1.3_MOSI
  N8: WeMos_D1_Mini1.D8, RFM95W1.2_MISO
  N9: WeMos_D1_Mini1.G, RFM95W1.8_GND
  N10: WeMos_D1_Mini1.RST, RFM95W1.6_RESET

custom parts:
  RFM95W LoRa Module: RF Transceiver by Hope RF. Well supported Arduino libraries are available. This Low Power Long Range Transceiver Module for the frequencies 868MHz and 915MHz and it is also available in other versions.
